# Fritzing sketch attiny85-radiohead-dht22-weather-sensor (saved by Fritzing 0.9.2b)
circuit board: 6.06586cm x 3.37477cm
breadboards: 1

parts:
  U1 = FS1000A - 433Mhz RF Transmitter [package=THT]
  U2 = attiny85 [package=dip]
  DHT1 = DHT22 Humidity and Temperature Sensor
  LED1 = LED - 5mm [color="Green (565nm)" package="5 mm [THT]"]
  LED2 = LED - 5mm [color="Red (633nm)" package="5 mm [THT]"]
  R2 = Resistor [tolerance=±5% resistance=470 package=THT]
  R3 = Resistor [tolerance=±5% resistance=10k package=THT]
  R4 = Resistor [tolerance=±5% resistance=4.7k package=THT]
  U3 = mystery part, 4 pins [chip_label="DC Boost"]
  BAT1 = Battery Holders [package=battery-aa-kit]
  BAT2 = Battery Holders [package=battery-aa-kit]
  BAT3 = Battery Holders [package=battery-aa-kit]
  R1 = Resistor [tolerance=±5% resistance=470 package=THT]

nets (from the breadboard view):
  N1: U1.DATA, U2.Pin_2, R1.Pin_0
  VCC: U1.VCC, U2.Pin_8, DHT1.VDD, R3.Pin_1, R4.Pin_1, U3.pin4
  GND: U1.GND, U2.Pin_4, DHT1.GND, LED1.cathode, LED2.cathode, U3.pin3
  N2: U2.Pin_1, R3.Pin_0
  N3: U2.Pin_3, R2.Pin_0
  N4: U2.Pin_6, DHT1.DATA, R4.Pin_0
  N5: U2.Pin_7, U3.pin1, BAT1.+
  N6: LED1.anode, R1.Pin_1
  N7: LED2.anode, R2.Pin_1
  N8: U3.pin2, BAT2.-
  N9: BAT1.-, BAT3.+
  N10: BAT2.+, BAT3.-

notes:
  DC Boost-Converter
  0,6-5V to 5V
  DHT22
  17cm antenna
  433MHz radio module
  green LED = transmitting
  red LED = status
  https://crycode.de/
  (c) 2017 Peter Müller

custom parts:
  FS1000A - 433Mhz RF Transmitter: This is 433Mhz RF transmitter with receiver kit for Arduino ARM MCU wireless Application environment: Remote control switch, receiver module, motorcycles, automobile anti-theft products, home security products, electric doors, shutter doors, windows, remote control socket, remote control LED, remote audio remote control electric doors, garage door remote control, remote control retractable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
